# Fritzing sketch plan (saved by Fritzing 0.9.0b)
stripboards: 1

parts:
  DC-DC-1_25V-26V1 = DC-DC-1.25V-26V
  ModeSwitch = SWITCH-DPDT [package=eg2211]
  RS232 = MAX232 TTL RS232 Adapter
  S1 = SWITCH-MOMENTARY-2 [package=tactile-switch-1101ne]
  WPS = SWITCH-MOMENTARY-2 [package=tactile-switch-1101ne]
  Reset = SWITCH-MOMENTARY-2 [package=tactile-switch-1101ne]
  R1 = Resistor [tolerance=±5% resistance=10k package=THT]
  R2 = Resistor [tolerance=±5% resistance=10k package=THT]  # not connected
  C1 = Capacitor Polarized [package=cpol-radial-100uf-25v]
  R4 = Resistor [tolerance=±5% resistance=10k package=THT]
  Q1 = PNP-Transistor [package="TO92 [THT]"]
  Q2 = NPN-Transistor [package="TO92 [THT]"]
  V2 = DC Power [voltage=5]  # not connected
  U1 = RELAY-SOLIDSTATE [package=relay-s108t02]
  U1_2 = ESP8266 WiFi Module [part_number=ESP8266]
  R6 = Resistor [tolerance=±5% resistance=10k package=THT]
  C2 = Capacitor Polarized [package=cpol-radial-100uf-25v]
  R8 = Resistor [tolerance=±5% resistance=1M package=THT]
  R7 = Resistor [tolerance=±5% resistance=220 package="1206 [SMD]"]
  R7_2 = Resistor [tolerance=±5% resistance=100k package=THT]
  R7_3 = Resistor [tolerance=±5% resistance=1k package=THT]
  R9 = Resistor [tolerance=±5% resistance=100k package=THT]

nets (from the breadboard view):
  N1: DC-DC-1_25V-26V1.IN+, U1.+
  GND: DC-DC-1_25V-26V1.OUT-, ModeSwitch.4, RS232.GND, WPS.2, Reset.2, U1_2.GND, R9.Pin_1
  N2: ModeSwitch.2, U1_2.RXD
  N3: ModeSwitch.3, S1.2, R9.Pin_0
  N4: ModeSwitch.6, RS232.RxD
  N5: ModeSwitch.5, U1_2.GPIO_0
  VCC: RS232.VCC, RS232.TxD, S1.1, R1.Pin_1, U1_2.VCC, U1_2.CH_PD, U1_2.TXD, C2.+, R8.Pin_1
  N6: WPS.1, R7.Pin_1, R7_2.Pin_1, R7_3.Pin_1
  N7: Reset.1, R1.Pin_0, U1_2.RST
  N8: C1.-, R4.Pin_0
  N9: R4.Pin_1, Q1.B
  N10: Q1.E, R6.Pin_0
  N11: Q1.C, Q2.E
  N12: Q2.B, R6.Pin_1
  N13: Q2.C, U1.-
  N14: C2.-, R8.Pin_0, R7.Pin_0, R7_2.Pin_0, R7_3.Pin_0

custom parts:
  ESP8266 WiFi Module: Generic WiFi Module based on the ESP8266 with onboard PCB antenna and UART communications
