# Fritzing sketch SwitchMoni (saved by Fritzing 0.9.3b)
stripboards: 1

parts:
  BAT1 = Battery Holders [package=battery-aa-kit]
  BAT2 = Battery Holders [package=battery-aa-kit]
  U1 = ESP8266 WiFi Module [part_number=ESP8266]
  3_5_Volt = Screw terminal - 2 pins [package=THT]
  R4 = Resistor [tolerance=±5% resistance=10k package=THT]
  IC1 = XOR Gatter 74HC86 [package="DIP (Dual Inline)"]
  R5 = Resistor [tolerance=±5% resistance=10k package=THT]
  WPS1 = Pushbutton [package="[SMD]"]
  R6 = Resistor [tolerance=±5% resistance=10k package=THT]
  SW1 = Screw terminal - 2 pins [package=THT]
  R7 = Resistor [tolerance=±5% resistance=10k package=THT]
  C1 = Tantalum Capacitor [capacitance=100nF package="C 6032 [SMD, tantalum]"]

nets (from the schematic view):
  N1: BAT1.+, BAT2.-
  GND: BAT1.-, U1.GND, 3_5_Volt.pin1, IC1.GND, WPS1.Pin_3, WPS1.Pin_4, SW1.pin2
  VCC: BAT2.+, U1.VCC, 3_5_Volt.pin2, R4.Pin_1, IC1.B4, IC1.VCC, R5.Pin_1, R6.Pin_1, C1.+
  N2: U1.RXD, R5.Pin_0, WPS1.Pin_1, WPS1.Pin_2
  N3: U1.RST, IC1.Y4
  N4: U1.GPIO_2, IC1.B3, R6.Pin_0, SW1.pin1, R7.Pin_0
  N5: U1.CH_PD, R4.Pin_0
  N6: IC1.A3, R7.Pin_1, C1.-
  N7: IC1.Y3, IC1.A4

custom parts:
  ESP8266 WiFi Module: Generic WiFi Module based on the ESP8266 with onboard PCB antenna and UART communications
  XOR Gatter 74HC86: 4 fach XOR Gatter
