# Fritzing sketch Electric (saved by Fritzing 0.9.3b)
stripboards: 1

parts:
  U1 = ESP8266 WiFi Module [part_number=ESP8266]
  LM2598DC1 = DC-DC-1.25V-26V
  R1 = Resistor [tolerance=±5% resistance=330 package=THT]
  IC1 = Microchip MCP23008 8-bit I/O expander [part_number=MCP23008 package="DIP (Dual Inline) [THT]"]
  R4 = Resistor [tolerance=±5% resistance=330 package=THT]
  R7 = Resistor [tolerance=±5% resistance=330 package=THT]
  R5 = Resistor [tolerance=±5% resistance=10k package=THT]
  R2 = Resistor [tolerance=±5% resistance=10k package=THT]
  R6 = Resistor [tolerance=±5% resistance=10k package=THT]
  R3 = Resistor [tolerance=±5% resistance=10k package=THT]
  WPS = Pushbutton [package="[SMD]"]
  RST = Pushbutton [package="[THT]"]
  PRG = SWITCH_SPDT [package=kps-1290]
  JP1 = Header 6 [package=molex-1x6-ra]
  Power_24Volt = Screw terminal - 2 pins [package=THT]
  MOSFET_Driver_3_3V_in3 = IRF520 MosFET Driver
  MOSFET_Driver_3_3V_in4 = IRF520 MosFET Driver
  MOSFET_Driver_3_3V_in0 = IRF520 MosFET Driver
  MOSFET_Driver_3_3V_in1 = IRF520 MosFET Driver
  MOSFET_Driver_3_3V_in2 = IRF520 MosFET Driver

nets:
  N1: U1.RXD, R1.Pin_0, WPS.Pin_1, WPS.Pin_2
  N2: U1.GPIO_0, R7.Pin_1, R6.Pin_0, PRG.P
  N3: U1.RST, IC1.Reset, R3.Pin_0, RST.Pin_1, RST.Pin_2
  N4: U1.GPIO_2, R4.Pin_1, R5.Pin_0
  N5: U1.CH_PD, R2.Pin_0
  GND: U1.GND, LM2598DC1.IN-, LM2598DC1.OUT-, IC1.A2, IC1.A0, IC1.VSS, WPS.Pin_3, WPS.Pin_4, RST.Pin_3, RST.Pin_4, PRG.O, JP1.6, Power_24Volt.pin1, MOSFET_Driver_3_3V_in3.Vin_GND, MOSFET_Driver_3_3V_in3.GND, MOSFET_Driver_3_3V_in4.Vin_GND, MOSFET_Driver_3_3V_in4.GND, MOSFET_Driver_3_3V_in0.Vin_GND, MOSFET_Driver_3_3V_in0.GND, MOSFET_Driver_3_3V_in1.Vin_GND, MOSFET_Driver_3_3V_in1.GND, MOSFET_Driver_3_3V_in2.Vin_GND, MOSFET_Driver_3_3V_in2.GND
  N6: U1.TXD, JP1.3
  N7: LM2598DC1.IN+, Power_24Volt.pin2, MOSFET_Driver_3_3V_in3.Vin_+, MOSFET_Driver_3_3V_in4.Vin_+, MOSFET_Driver_3_3V_in0.Vin_+, MOSFET_Driver_3_3V_in1.Vin_+, MOSFET_Driver_3_3V_in2.Vin_+
  VCC: LM2598DC1.OUT+, IC1.A1, IC1.VDD, R5.Pin_1, R2.Pin_1, R6.Pin_1, R3.Pin_1, MOSFET_Driver_3_3V_in3.VCC, MOSFET_Driver_3_3V_in4.VCC, MOSFET_Driver_3_3V_in0.VCC, MOSFET_Driver_3_3V_in1.VCC, MOSFET_Driver_3_3V_in2.VCC
  N8: R1.Pin_1, JP1.2
  N9: IC1.SCL, R4.Pin_0
  N10: IC1.SDA, R7.Pin_0
  N11: IC1.GP0, MOSFET_Driver_3_3V_in0.SIG
  N12: IC1.GP1, MOSFET_Driver_3_3V_in1.SIG
  N13: IC1.GP2, MOSFET_Driver_3_3V_in2.SIG
  N14: IC1.GP3, MOSFET_Driver_3_3V_in3.SIG
  N15: IC1.GP4, MOSFET_Driver_3_3V_in4.SIG

custom parts:
  ESP8266 WiFi Module: Generic WiFi Module based on the ESP8266 with onboard PCB antenna and UART communications
  Microchip MCP23008 8-bit I/O expander: Provides 8-bit, general purpose, parallel I/O expansion for I2C bus. Datasheet: http://ww1.microchip.com/downloads/en/devicedoc/21919e.pdf
